# Fritzing sketch Kegabyte_v_1.0 (saved by Fritzing 0.9.0b)
circuit board: 10cm x 6cm
breadboards: 2

parts:
  Crystal_1 = Crystal [frequency="16 Mhz" package=THT]
  U1 = atmega328 [package=dip]
  Red_Pot = Rotary Potentiometer (Large) [maximum_resistance=10kΩ package=THT]
  Green_Pot = Rotary Potentiometer (Large) [maximum_resistance=10kΩ package=THT]
  Blue_Pot = Rotary Potentiometer (Large) [maximum_resistance=10kΩ package=THT]
  Flow_Sensor#1 = male pin header, 3 pins [form="♂ (male)"]
  Flow_Sensor_#2 = male pin header, 3 pins [form="♂ (male)"]
  22pf_Cermaic_Cap_#1 = Ceramic Capacitor [capacitance=100nF package="100 mil [THT, multilayer]"]
  22pf_Cermaic_Cap_#2 = Ceramic Capacitor [capacitance=100nF package="100 mil [THT, multilayer]"]
  R1 = Resistor [tolerance=±5% resistance=10k package=THT]
  R2 = Resistor [tolerance=±5% resistance=10k package=THT]
  DHT1 = Humidity and Temperature Sensor DHT11
  DHT2 = Humidity and Temperature Sensor DHT11
  Q1 = Basic FET N-Channel [package="TO220 [THT]"]
  Q2 = Basic FET N-Channel [package="TO220 [THT]"]
  Q3 = Basic FET N-Channel [package="TO220 [THT]"]
  I2C_EEPROM = 24LC256 [package=THT]
  RGB_LED_STRIP = RGB LED (com. anode, rbg) [package="5 mm [THT]"]
  5V_Regulator = Voltage Regulator - 5V [package="TO220 [THT]"]
  Power_plug1 = Power plug
  LCD_Header = male pin header, 4 pins [form="♂ (male)"]

nets (from the schematic view):
  N1: Crystal_1.pin_0, U1.XLAT2, 22pf_Cermaic_Cap_#2.1
  N2: Crystal_1.pin_1, U1.XLAT1, 22pf_Cermaic_Cap_#1.1
  N3: U1.D3_(PWM), Q3.gate
  N4: U1.D4, Q2.gate
  N5: U1.VCC, U1.AVCC, U1.AREF, Red_Pot.leg1, Green_Pot.leg1, Flow_Sensor#1.pin3, Flow_Sensor_#2.pin3, I2C_EEPROM.+V, 5V_Regulator.output_voltage, LCD_Header.pin2
  GND: U1.GND, Red_Pot.leg2, Green_Pot.leg2, Blue_Pot.leg2, Flow_Sensor#1.pin1, Flow_Sensor_#2.pin1, 22pf_Cermaic_Cap_#1.0, 22pf_Cermaic_Cap_#2.0, DHT1.GND_2, DHT2.GND_2, Q1.drain, Q2.drain, Q3.drain, I2C_EEPROM.A0, I2C_EEPROM.A1, I2C_EEPROM.A2, I2C_EEPROM.0V, I2C_EEPROM.WP_-_Write_Protect, 5V_Regulator.GND, Power_plug1.GND, LCD_Header.pin1
  N6: U1.D5_(PWM), Q1.gate
  N7: U1.D7, Flow_Sensor_#2.pin2
  N8: U1.D8, Flow_Sensor#1.pin2
  N9: U1.D9_(PWM), R2.Pin_0
  N10: U1.D10_(PWM), U1.A0, R1.Pin_0
  N11: U1.A1, Red_Pot.wiper
  N12: U1.A2, Green_Pot.wiper
  N13: U1.A3, Blue_Pot.wiper
  N14: U1.A4, I2C_EEPROM.SDA_-_I2C_Data, LCD_Header.pin3
  N15: U1.A5, I2C_EEPROM.SCL_-_I2C_Clock, LCD_Header.pin4
  VCC: Blue_Pot.leg1, R2.Pin_1, DHT1.Vcc, DHT2.Vcc, DHT2.Data-signal, RGB_LED_STRIP.common_anode
  N16: R1.Pin_1, DHT1.Data-signal
  N17: Q1.source, RGB_LED_STRIP.red_cathode
  N18: Q2.source, RGB_LED_STRIP.green_cathode
  N19: Q3.source, RGB_LED_STRIP.blue_cathode
  12V: 5V_Regulator.input_voltage, Power_plug1.VCC

notes:
  Kegerator Monitor - Lance Gundersen, Home Bar Lighting, Monitoring and Entertainment, 1
  Input Jack Represents Input Voltage!
  GND
  VCC
  SDA
  SCL
  Kegerator Monitor - Lance Gundersen
  Green Pot
  Red Pot
  Blue Pot
  DHT 1
  DHT 2
  Flow 2
  Flow 1
  LCD
  RGB LED STRIP

custom parts:
  Humidity and Temperature Sensor DHT11: Digital relative humidity & temperature sensor DHT11
