# Fritzing sketch Kegabyte_v_1.0_ArduinoBreadboard (saved by Fritzing 0.9.0b)
circuit board: 10cm x 6cm
breadboards: 1

parts:
  Red_Pot = Rotary Potentiometer (Large) [maximum_resistance=10kΩ package=THT]
  Green_Pot = Rotary Potentiometer (Large) [maximum_resistance=10kΩ package=THT]
  Blue_Pot = Rotary Potentiometer (Large) [maximum_resistance=10kΩ package=THT]
  Flow_Sensor#1 = male pin header, 3 pins [form="♂ (male)"]
  Flow_Sensor_#2 = male pin header, 3 pins [form="♂ (male)"]
  R1 = Resistor [tolerance=±5% resistance=10k package=THT]
  R2 = Resistor [tolerance=±5% resistance=10k package=THT]
  DHT1 = Humidity and Temperature Sensor DHT11
  DHT2 = Humidity and Temperature Sensor DHT11
  Q1 = Basic FET N-Channel [package="TO220 [THT]"]
  Q2 = Basic FET N-Channel [package="TO220 [THT]"]
  Q3 = Basic FET N-Channel [package="TO220 [THT]"]
  I2C_EEPROM = 24LC256 [package=THT]
  RGB_LED_STRIP = RGB LED (com. anode, rbg) [package="5 mm [THT]"]
  LCD_Header = male pin header, 4 pins [form="♂ (male)"]
  Part2 = Arduino Uno (Rev3)

nets (from the breadboard view):
  N1: Red_Pot.leg1, Green_Pot.leg1, Blue_Pot.leg1, I2C_EEPROM.+V, LCD_Header.pin2
  N2: Red_Pot.wiper, Part2.A1
  N3: Red_Pot.leg2, Green_Pot.leg2, Blue_Pot.leg2, I2C_EEPROM.WP_-_Write_Protect, LCD_Header.pin1
  N4: Green_Pot.wiper, Part2.A2
  N5: Blue_Pot.wiper, Part2.A3
  N6: Flow_Sensor#1.pin1, Flow_Sensor_#2.pin1, DHT1.GND_2, DHT2.GND_2, Q1.source, Q2.source, Q3.source, I2C_EEPROM.A0, I2C_EEPROM.A1, I2C_EEPROM.A2, I2C_EEPROM.0V, RGB_LED_STRIP.common_anode
  N7: Flow_Sensor#1.pin2, Part2.D8
  VCC: Flow_Sensor#1.pin3, Flow_Sensor_#2.pin3, R1.Pin_0, R2.Pin_0, DHT1.Vcc, DHT2.Vcc
  N8: Flow_Sensor_#2.pin2, Part2.D7
  N9: R1.Pin_1, DHT1.Data-signal, Part2.D10_PWM/SS
  N10: R2.Pin_1, DHT2.Data-signal, Part2.D9_PWM
  N11: Q1.gate, Part2.D5_PWM
  N12: Q1.drain, RGB_LED_STRIP.red_cathode
  N13: Q2.gate, Part2.D4
  N14: Q2.drain, RGB_LED_STRIP.green_cathode
  N15: Q3.gate, Part2.D3_PWM
  N16: Q3.drain, RGB_LED_STRIP.blue_cathode
  N17: I2C_EEPROM.SDA_-_I2C_Data, LCD_Header.pin3, Part2.A4/SDA
  N18: I2C_EEPROM.SCL_-_I2C_Clock, LCD_Header.pin4, Part2.A5/SCL

notes:
  Kegerator Monitor - Lance Gundersen, Home Bar Lighting, Monitoring and Entertainment, 1
  GND
  VCC
  SDA
  SCL
  Kegerator Monitor - Lance Gundersen
  Green Pot
  Red Pot
  Blue Pot
  DHT 1
  DHT 2
  Flow 2
  Flow 1
  LCD
  RGB LED STRIP

custom parts:
  Humidity and Temperature Sensor DHT11: Digital relative humidity & temperature sensor DHT11
